# Fritzing sketch sketch (saved by Fritzing 0.9.5d)

parts:
  Part1 = Adafruit HUZZAH32 ESP32 Feather [part_number="Adafruit #3405"]
  Part2 = HC-SR501 Body Sensor Module
  U1 = LIPO-110mAh [package=lipo-110]  # not connected

nets:
  GND: Part1.GND, Part2.GND
  3.3V: Part1.3.3V, Part2.VCC
  N1: Part1.IO15_A8, Part2.OUT

custom parts:
  HC-SR501 Body Sensor Module: Pyroelectric Infrared PIR Motion Sensor Detector Module
